// Digital circuit 4bit_ALU.dlogic.dig as structural Verilog
module _4bit_ALU_dlogic (
  input  [3:0] A,
  input  [3:0] B,
  input  [2:0] Control,
  input  CinAdd,
  input  CinSub,
  output [3:0] Result,
  output SLT_Output,
  output CoutAdd,
  output ZeroFlag
);

  wire [3:0] _4bit_and_operation_1_output, _4bit_full_adder_1_sum, _4bit_or_operation_1_output,
       _4bit_subtractor_1_sum, _4bit_xor_operation_1_output;

  _4bit_full_adder _4bit_full_adder_1 (.A(A), .B(B), .Cin(CinAdd), .Sum(_4bit_full_adder_1_sum), .Cout(CoutAdd));
  _4bit_subtractor _4bit_subtractor_1 (.B(B), .A(A), .Cin(CinSub), .Sum(_4bit_subtractor_1_sum));
  _4bit_AND_operation _4bit_and_operation_1 (.A(A), .B(B), .Output(_4bit_and_operation_1_output));
  _4bit_OR_operation _4bit_or_operation_1 (.A(A), .B(B), .Output(_4bit_or_operation_1_output));
  _4bit_XOR_operation _4bit_xor_operation_1 (.A(A), .B(B), .Output(_4bit_xor_operation_1_output));
  _4bit_SLT_logic _4bit_slt_logic_1 (.A(A), .B(B), .Cin(CinSub), .Output(SLT_Output));
  Multiplexer #(.Bits(4), .Selector_Bits(3)) multiplexer_1 (
    .sel(Control), .in_0(_4bit_full_adder_1_sum), .in_1(_4bit_subtractor_1_sum),
    .in_2(_4bit_and_operation_1_output), .in_3(_4bit_or_operation_1_output),
    .in_4(_4bit_xor_operation_1_output), .in_5(4'b0000), .in_6(4'b0000), .in_7(4'b0000), .out(Result));
  _4bit_ZeroFlag _4bit_zeroflag_1 (.In(_4bit_subtractor_1_sum), .Out(ZeroFlag));

  // Notes on the sheet:
  //   CinSub: default 1
endmodule
