// Digital circuit 4bit_AND_operation.dig as structural Verilog
module _4bit_AND_operation (
  input  [3:0] A,
  input  [3:0] B,
  output [3:0] Output
);

  assign Output = A & B;  // And and_1, 4 bits wide
endmodule
