// Digital circuit 4bit_OR_operation.dig as structural Verilog
module _4bit_OR_operation (
  input  [3:0] A,
  input  [3:0] B,
  output [3:0] Output
);

  assign Output = A | B;  // Or or_1, 4 bits wide
endmodule
