// Digital circuit 4bit_Processor.dlogic.dig as structural Verilog
module _4bit_Processor_dlogic (
  input  in_4,
  input  [3:0] in_5,
  input  [3:0] in_6,
  input  in_7,
  input  [1:0] in_8,
  input  clk,
  input  [1:0] in_10,
  input  clk_2,
  output out_1,
  output out_2,
  output out_3,
  output [3:0] out_12,
  output out_13,
  output out_14,
  output out_15,
  output [3:0] out_16,
  output [3:0] out_17
);

  wire controlunit1_1_and, controlunit1_1_il, controlunit1_1_or, controlunit1_1_slt, controlunit1_1_sub,
       controlunit1_1_xor, instructionreg_1_a, instructionreg_1_b, instructionreg_1_c, instructionreg_1_d;
  wire [0:0] fde_1_fetch;
  wire [1:0] controlunit1_1_readr_1, controlunit1_1_readr_2, controlunit1_1_we, controlunit1_1_wr;
  wire [2:0] or_1_out;
  wire [3:0] memorymodule_1_out, multiplexer_1_out, programcounter_1_out;

  ProgramCounter programcounter_1 (.CLK(clk), .R_W_C(in_8), .Address(in_6), .I_L(in_7), .Out(programcounter_1_out));
  MemoryModule memorymodule_1 (
    .R_W_C(in_10), .CLK(clk_2), .Address(programcounter_1_out), .Data(in_5), .Out(memorymodule_1_out));
  InstructionReg instructionreg_1 (
    .Operation(memorymodule_1_out), .Con({1'b0, fde_1_fetch[0]}), .CLK(clk_2), .A(instructionreg_1_a),
    .B(instructionreg_1_b), .C(instructionreg_1_c), .D(instructionreg_1_d));
  ControlUnit1 controlunit1_1 (
    .A(instructionreg_1_a), .B(instructionreg_1_b), .C(instructionreg_1_c), .D(instructionreg_1_d),
    .WR(controlunit1_1_wr), .WE(controlunit1_1_we), .IL(controlunit1_1_il), .ADD(out_13),
    .SUB(controlunit1_1_sub), .AND(controlunit1_1_and), .OR(controlunit1_1_or), .XOR(controlunit1_1_xor),
    .ReadR_2(controlunit1_1_readr_2), .ReadR_1(controlunit1_1_readr_1), .SLT(controlunit1_1_slt));
  FDE fde_1 (.CLK(clk_2), .In(in_4), .Fetch(fde_1_fetch[0]), .Decode(out_14), .Execute(out_15));
  Multiplexer #(.Bits(4)) multiplexer_1 (
    .sel(controlunit1_1_il), .in_0(out_12), .in_1(memorymodule_1_out), .out(multiplexer_1_out));
  RegistersFile registersfile_1 (
    .Read1(controlunit1_1_readr_1), .Read2(controlunit1_1_readr_2), .CLK(clk_2), .WD(multiplexer_1_out),
    .WR(controlunit1_1_wr), .WE(controlunit1_1_we), .Data1(out_17), .Data2(out_16));
  or or_1 (or_1_out[0], controlunit1_1_sub, controlunit1_1_or, controlunit1_1_slt);
  or or_2 (or_1_out[1], controlunit1_1_and, controlunit1_1_or);
  or or_3 (or_1_out[2], controlunit1_1_xor, controlunit1_1_slt);
  // _4bit_ALU_dlogic _4bit_alu_dlogic_1: pin names not known; wires that end beside it: out_17, out_16, or_1_out, out_12, out_1, out_2, out_3
endmodule
