// Digital circuit 4bit_SLT_logic.dig as structural Verilog
module _4bit_SLT_logic (
  input  [3:0] A,
  input  [3:0] B,
  input  Cin,
  output Output
);

  wire [2:0] _4bit_subtractor_1_sum;

  _4bit_subtractor _4bit_subtractor_1 (.B(B), .A(A), .Cin(Cin), .Sum({Output, _4bit_subtractor_1_sum}));

  // Notes on the sheet:
  //   Cin: default 1
endmodule
