// Digital circuit 4bit_XOR_operation.dig as structural Verilog
module _4bit_XOR_operation (
  input  [3:0] A,
  input  [3:0] B,
  output [3:0] Output
);

  assign Output = A ^ B;  // XOr xor_1, 4 bits wide
endmodule
