// Digital circuit ControlUnit1.dig as structural Verilog
module ControlUnit1 (
  input  A,
  input  B,
  input  C,
  input  D,
  output [1:0] WR,
  output [1:0] WE,
  output IL,
  output ADD,
  output SUB,
  output AND,
  output OR,
  output XOR,
  output [1:0] ReadR_2,
  output [1:0] ReadR_1,
  output SLT
);

  wire and_5_out, and_6_out, and_7_out, and_8_out, not_1_out, not_2_out, not_3_out, not_4_out, not_5_out;

  and and_1 (SLT, A, B, C, not_3_out);
  and and_2 (OR, A, B, not_5_out, not_3_out);
  and and_3 (AND, A, not_2_out, C, D);
  not not_1 (not_1_out, A);
  not not_2 (not_2_out, B);
  not not_3 (not_3_out, D);
  not not_4 (not_4_out, A);
  not not_5 (not_5_out, C);
  and and_4 (ReadR_1[0], not_4_out, B, C, D);
  and and_5 (and_5_out, not_1_out, not_2_out, C);
  and and_6 (and_6_out, A, not_5_out, not_3_out);
  and and_7 (and_7_out, not_1_out, C);
  and and_8 (and_8_out, not_1_out, D);
  or or_1 (WR[0], and_5_out, and_6_out);
  or or_2 (IL, and_7_out, and_8_out);
  or or_3 (WE[0], A, C, D);
  and and_9 (XOR, A, B, not_5_out, D);
  and and_10 (ADD, A, not_2_out, not_5_out, D);
  and and_11 (SUB, A, not_2_out, C, not_3_out);

  assign ReadR_1[1] = 1'b0;
  assign ReadR_2 = 2'b01;
  assign WE[1] = 1'b0;
  assign WR[1] = 1'b0;
endmodule
