// Digital circuit FDE.dig as structural Verilog
module FDE (
  input  CLK,
  input  In,
  output Fetch,
  output Decode,
  output Execute
);

  wire and_1_out, and_2_out, and_3_out, and_4_out, Dlsb_q, Dmsb_q, not_1_out, not_2_out, not_3_out,
       not_4_out, not_5_out, not_6_out, or_1_out, or_2_out;

  not not_1 (not_1_out, Dmsb_q);
  not not_2 (not_2_out, Dlsb_q);
  and and_1 (and_1_out, Dmsb_q, not_3_out);
  not not_3 (not_3_out, In);
  and and_2 (and_2_out, Dlsb_q, In);
  and and_3 (and_3_out, not_1_out, not_2_out, In);
  and and_4 (and_4_out, Dlsb_q, not_4_out);
  not not_4 (not_4_out, In);
  or or_1 (or_1_out, and_1_out, and_2_out);
  or or_2 (or_2_out, and_3_out, and_4_out);
  D_FF Dmsb (.D(or_1_out), .C(CLK), .Q(Dmsb_q));  // open: nQ
  D_FF Dlsb (.D(or_2_out), .C(CLK), .Q(Dlsb_q));  // open: nQ
  not not_5 (not_5_out, Dmsb_q);
  not not_6 (not_6_out, Dlsb_q);
  and and_5 (Fetch, not_5_out, not_6_out);
  and and_6 (Decode, not_5_out, Dlsb_q);
  and and_7 (Execute, Dmsb_q, not_6_out);
endmodule
