// Digital circuit InstructionReg.dig as structural Verilog
module InstructionReg (
  input  CLK,
  input  [1:0] Con,
  input  [3:0] Operation,
  output B,
  output A,
  output C,
  output D
);

  Register register_1 (.In(Operation), .Con(Con), .CLK(CLK), .O({A, B, C, D}));
endmodule
