// Digital circuit MemoryModule.dig as structural Verilog
module MemoryModule (
  input  [1:0] R_W_C,
  input  CLK,
  input  [3:0] Address,
  input  [3:0] Data,
  output [3:0] Out
);

  wire [1:0] demultiplexer_1_out_0, demultiplexer_1_out_1, demultiplexer_1_out_2, demultiplexer_1_out_3,
       demultiplexer_1_out_4, demultiplexer_1_out_5, demultiplexer_1_out_6, demultiplexer_1_out_7,
       demultiplexer_1_out_8, demultiplexer_1_out_9, demultiplexer_1_out_10, demultiplexer_1_out_11,
       demultiplexer_1_out_12, demultiplexer_1_out_13, demultiplexer_1_out_14, demultiplexer_1_out_15;
  wire [3:0] _0_o, _1_o, _2_o, _3_o, _4_o, _5_o, _6_o, _7_o, _8_o, _9_o, _10_o, _11_o, _12_o, _13_o, _14_o,
       _15_o, demultiplexer_2_out_0, demultiplexer_2_out_1, demultiplexer_2_out_2, demultiplexer_2_out_3,
       demultiplexer_2_out_4, demultiplexer_2_out_5, demultiplexer_2_out_6, demultiplexer_2_out_7,
       demultiplexer_2_out_8, demultiplexer_2_out_9, demultiplexer_2_out_10, demultiplexer_2_out_11,
       demultiplexer_2_out_12, demultiplexer_2_out_13, demultiplexer_2_out_14, demultiplexer_2_out_15;

  Demultiplexer #(.Selector_Bits(4), .Bits(2)) demultiplexer_1 (
    .sel(Address), .in(R_W_C), .out_0(demultiplexer_1_out_0), .out_1(demultiplexer_1_out_1),
    .out_2(demultiplexer_1_out_2), .out_3(demultiplexer_1_out_3), .out_4(demultiplexer_1_out_4),
    .out_5(demultiplexer_1_out_5), .out_6(demultiplexer_1_out_6), .out_7(demultiplexer_1_out_7),
    .out_8(demultiplexer_1_out_8), .out_9(demultiplexer_1_out_9), .out_10(demultiplexer_1_out_10),
    .out_11(demultiplexer_1_out_11), .out_12(demultiplexer_1_out_12), .out_13(demultiplexer_1_out_13),
    .out_14(demultiplexer_1_out_14), .out_15(demultiplexer_1_out_15));
  Demultiplexer #(.Selector_Bits(4), .Bits(4)) demultiplexer_2 (
    .sel(Address), .in(Data), .out_0(demultiplexer_2_out_0), .out_1(demultiplexer_2_out_1),
    .out_2(demultiplexer_2_out_2), .out_3(demultiplexer_2_out_3), .out_4(demultiplexer_2_out_4),
    .out_5(demultiplexer_2_out_5), .out_6(demultiplexer_2_out_6), .out_7(demultiplexer_2_out_7),
    .out_8(demultiplexer_2_out_8), .out_9(demultiplexer_2_out_9), .out_10(demultiplexer_2_out_10),
    .out_11(demultiplexer_2_out_11), .out_12(demultiplexer_2_out_12), .out_13(demultiplexer_2_out_13),
    .out_14(demultiplexer_2_out_14), .out_15(demultiplexer_2_out_15));
  Register _0 (.In(demultiplexer_2_out_0), .Con(demultiplexer_1_out_0), .CLK(CLK), .O(_0_o));
  Register _1 (.In(demultiplexer_2_out_1), .Con(demultiplexer_1_out_1), .CLK(CLK), .O(_1_o));
  Register _2 (.In(demultiplexer_2_out_2), .Con(demultiplexer_1_out_2), .CLK(CLK), .O(_2_o));
  Register _3 (.In(demultiplexer_2_out_3), .Con(demultiplexer_1_out_3), .CLK(CLK), .O(_3_o));
  Register _4 (.In(demultiplexer_2_out_4), .Con(demultiplexer_1_out_4), .CLK(CLK), .O(_4_o));
  Register _5 (.In(demultiplexer_2_out_5), .Con(demultiplexer_1_out_5), .CLK(CLK), .O(_5_o));
  Register _6 (.In(demultiplexer_2_out_6), .Con(demultiplexer_1_out_6), .CLK(CLK), .O(_6_o));
  Register _7 (.In(demultiplexer_2_out_7), .Con(demultiplexer_1_out_7), .CLK(CLK), .O(_7_o));
  Register _8 (.In(demultiplexer_2_out_8), .Con(demultiplexer_1_out_8), .CLK(CLK), .O(_8_o));
  Register _9 (.In(demultiplexer_2_out_9), .Con(demultiplexer_1_out_9), .CLK(CLK), .O(_9_o));
  Register _10 (.In(demultiplexer_2_out_10), .Con(demultiplexer_1_out_10), .CLK(CLK), .O(_10_o));
  Register _11 (.In(demultiplexer_2_out_11), .Con(demultiplexer_1_out_11), .CLK(CLK), .O(_11_o));
  Register _12 (.In(demultiplexer_2_out_12), .Con(demultiplexer_1_out_12), .CLK(CLK), .O(_12_o));
  Register _13 (.In(demultiplexer_2_out_13), .Con(demultiplexer_1_out_13), .CLK(CLK), .O(_13_o));
  Register _14 (.In(demultiplexer_2_out_14), .Con(demultiplexer_1_out_14), .CLK(CLK), .O(_14_o));
  Register _15 (.In(demultiplexer_2_out_15), .Con(demultiplexer_1_out_15), .CLK(CLK), .O(_15_o));
  Multiplexer #(.Selector_Bits(4), .Bits(4)) multiplexer_1 (
    .sel(Address), .in_0(_0_o), .in_1(_1_o), .in_2(_2_o), .in_3(_3_o), .in_4(_4_o), .in_5(_5_o), .in_6(_6_o),
    .in_7(_7_o), .in_8(_8_o), .in_9(_9_o), .in_10(_10_o), .in_11(_11_o), .in_12(_12_o), .in_13(_13_o),
    .in_14(_14_o), .in_15(_15_o), .out(Out));
endmodule
