// Digital circuit ProgramCounter.dig as structural Verilog
module ProgramCounter (
  input  CLK,
  input  [1:0] R_W_C,
  input  [3:0] Address,
  input  I_L,
  output [3:0] Out
);

  wire [3:0] multiplexer_1_out, undriven;

  Multiplexer #(.Bits(4)) multiplexer_1 (.sel(I_L), .in_0(undriven), .in_1(Address), .out(multiplexer_1_out));
  Register register_1 (.In(multiplexer_1_out), .Con(R_W_C), .CLK(CLK), .O(Out));
  _4bit_full_adder _4bit_full_adder_1 (.A(Out), .B(4'b0001), .Cin(1'b0));  // open: Sum, Cout
endmodule
