// Digital circuit RegistersFile.dig as structural Verilog
module RegistersFile (
  input  [1:0] Read1,
  input  [1:0] Read2,
  input  CLK,
  input  [3:0] WD,
  input  [1:0] WR,
  input  [1:0] WE,
  output [3:0] Data1,
  output [3:0] Data2
);

  wire [1:0] demultiplexer_1_out_0, demultiplexer_1_out_1, demultiplexer_1_out_2;
  wire [3:0] A_o, B_o, demultiplexer_2_out_0, demultiplexer_2_out_1, demultiplexer_2_out_2,
       demultiplexer_2_out_3;

  Demultiplexer #(.Selector_Bits(2), .Bits(2)) demultiplexer_1 (
    .sel(WR), .in(WE), .out_0(demultiplexer_1_out_0), .out_1(demultiplexer_1_out_1),
    .out_2(demultiplexer_1_out_2), .out_3(demultiplexer_1_out_2));
  Demultiplexer #(.Selector_Bits(2), .Bits(4)) demultiplexer_2 (
    .sel(WR), .in(WD), .out_0(demultiplexer_2_out_0), .out_1(demultiplexer_2_out_1),
    .out_2(demultiplexer_2_out_2), .out_3(demultiplexer_2_out_3));
  Register A (.In(demultiplexer_2_out_0), .Con(demultiplexer_1_out_0), .CLK(CLK), .O(A_o));
  Register B (.In(demultiplexer_2_out_1), .Con(demultiplexer_1_out_1), .CLK(CLK), .O(B_o));
  Multiplexer #(.Selector_Bits(2), .Bits(4)) multiplexer_1 (
    .sel(Read1), .in_0(A_o), .in_1(B_o), .in_2(4'b0000), .in_3(4'b0000), .out(Data1));
  Multiplexer #(.Selector_Bits(2), .Bits(4)) multiplexer_2 (
    .sel(Read2), .in_0(A_o), .in_1(B_o), .in_2(4'b0000), .in_3(4'b0000), .out(Data2));
  // also tied to GND on the sheet: {demultiplexer_1_out_2[0], demultiplexer_1_out_2[1], demultiplexer_2_out_2[0], demultiplexer_2_out_2[1], demultiplexer_2_out_2[2], demultiplexer_2_out_2[3], demultiplexer_2_out_3[0], demultiplexer_2_out_3[1], demultiplexer_2_out_3[2], demultiplexer_2_out_3[3]}
endmodule
